# Fritzing sketch EdgeDeviceArduinoNano (saved by Fritzing 0.9.3b)
circuit board: 9.04382cm x 6.46399cm
perfboards: 1

parts:
  Part2 = NRF24L01+ Breakout Board
  PC817_optocoupler = TLP621 [package=THT]
  R5 = Resistor [tolerance=±5% resistance=220 package=THT]
  Arduino_Nano = Arduino Nano (Rev3.0) [part_number=U1]
  10uf_capacitor = Electrolytic Capacitor [capacitance=10µF package="100 mil [THT, electrolytic]"]
  R7 = Resistor [tolerance=±5% resistance=220 package=THT]
  2_pin_header = Header 2 [package=molex-1x2_lock]
  LED1 = LED - 5mm [color="Green (565nm)" package="5 mm [THT]"]
  Power_Supply_Connector = Hirose DF13 Series Header [part_number="VIN 7-12v" package=DF13A-2P-1.25H]

nets:
  N1: Part2.GND, 10uf_capacitor.-
  VCC: Part2.VCC, Arduino_Nano.3V3, 10uf_capacitor.+
  N2: Part2.CE, Arduino_Nano.D9
  N3: Part2.CS, Arduino_Nano.D10
  N4: Part2.SCK, Arduino_Nano.D13/SCK
  N5: Part2.MOSI, Arduino_Nano.D11/MOSI
  N6: Part2.MISO, Arduino_Nano.D12/MISO
  N7: PC817_optocoupler.Pin_1, R5.Pin_1
  GND: PC817_optocoupler.Pin_2, Arduino_Nano.GND, LED1.cathode, Power_Supply_Connector.2
  N8: PC817_optocoupler.Pin_4, 2_pin_header.2
  N9: PC817_optocoupler.Pin_3, 2_pin_header.1
  N10: R5.Pin_0, Arduino_Nano.D2
  N11: Arduino_Nano.D3, R7.Pin_0
  N12: Arduino_Nano.VIN, Power_Supply_Connector.1
  N13: R7.Pin_1, LED1.anode
